# Fritzing sketch drone_circuit (saved by Fritzing 0.8.5b)
circuit board: 6cm x 6cm
breadboards: 1

parts:
  R1 = Resistor [tolerance=±5% resistance=220 package=THT]
  D1 = Diode [package=diode-1n4001]
  M2 = DC Motor
  R2 = Resistor [tolerance=±5% resistance=220 package=THT]
  M3 = DC Motor
  Q3 = NPN-Transistor [package="TO92 [THT]"]
  Q4 = NPN-Transistor [package="TO92 [THT]"]
  R3 = Resistor [tolerance=±5% resistance=220 package=THT]
  GY2 = MPU-6050 Board GY-521 [form="♀ (female)" package=THT]
  D2 = Diode [package=diode-1n4001]
  C5 = Capacitor Polarized [package=panasonic_c]
  C6 = Capacitor Polarized [package=panasonic_c]
  C7 = Capacitor Polarized [package=panasonic_c]
  C8 = Capacitor Polarized [package=panasonic_c]
  JP2 = Header 2 [package=jst-2-pth-kit]
  D3 = Diode [package=diode-1n4001]
  R4 = Resistor [tolerance=±5% resistance=220 package=THT]
  Q1 = NPN-Transistor [package="TO92 [THT]"]
  M4 = DC Motor
  D4 = Diode [package=diode-1n4001]
  Part1 = Arduino Pro Mini v13
  M1 = DC Motor
  Q2 = NPN-Transistor [package="TO92 [THT]"]

nets (from the schematic view):
  GND: R1.Pin_0, R2.Pin_0, Q3.E, R3.Pin_0, R4.Pin_1, Q1.E, Q2.E
  N1: R1.Pin_1, Q1.B, Part1.D9_PWM
  N2: D1.A, C6.+, Q1.C, M1.pin_1
  N3: D1.C, M2.pin_1, M3.pin_1, Q4.E, GY2.pin1, D2.C, C5.-, C6.-, C7.-, C8.-, JP2.2, D3.C, M4.pin_2, D4.C, Part1.VCC, M1.pin_2
  N4: M2.pin_2, D2.A, C8.+, Q2.C
  N5: R2.Pin_1, Part1.D6_PWM, Q2.B
  N6: M3.pin_2, Q3.C, C7.+, D3.A
  N7: Q3.B, R3.Pin_1, Part1.D10_PWM/SS
  N8: Q4.B, R4.Pin_0, Part1.D3_PWM
  N9: Q4.C, C5.+, M4.pin_1, D4.A
  N10: GY2.pin2, JP2.1, Part1.GND
  N11: GY2.pin3, Part1.A5
  N12: GY2.pin4, Part1.A4
  N13: GY2.pin8, Part1.D4

custom parts:
  MPU-6050 Board GY-521: Acelerometro y Giroscopio MPU-6050 Board GY-521
